// Logisim project 16BitCPU.circ as structural Verilog: 7 circuits, main circuit main
module CLOCK (
  input  CLK_SWITCH,
  input  CLK_STEP,
  output CLK
);

  wire and_1_out, and_2_out, clock_1_out, not_1_out;

  Clock clock_1 (.out(clock_1_out));
  Pull_Resistor pull_resistor_1 (.node(CLK_SWITCH));
  Pull_Resistor pull_resistor_2 (.node(CLK_STEP));
  and and_1 (and_1_out, clock_1_out, not_1_out);
  not not_1 (not_1_out, CLK_SWITCH);
  and and_2 (and_2_out, CLK_SWITCH, CLK_STEP);
  or or_1 (CLK, and_1_out, and_2_out);
endmodule

module main (
);

  wire A_IN, A_OUT, A_RST, alu_1_cf, alu_1_zf, B_IN, B_OUT, B_RST, button_1_out, EO, F_RST, FI, J, O_IN,
       O_RST, output_7segment_1_neg, PC_OUT, PCE, SU, switch_1_p2, switch_2_p2, TWOS;
  wire [15:0] alu_1_leds, bus_dipswitch_1_bus_out, program_counter_1_leds, register_1_a_bus, register_1_leds,
       register_2_a_bus, register_2_leds, undriven;
  wire [17:16] clock_1_clk;
  wire [31:0] output_7segment_1__7segment;

  // Switch switch_1: pin names not known; wires that end beside it: 1'b1, switch_1_p2
  Button button_1 (.out(button_1_out));
  Button button_2 (.out(clock_1_clk[17]));
  // DipSwitch #(.NSwitches(16)) dipswitch_1: pin names not known; wires that end beside it: undriven[15], undriven[14], undriven[13], undriven[12], undriven[11], undriven[10], undriven[9], undriven[8], undriven[7], undriven[6], undriven[5], undriven[4]
  // Switch switch_2: pin names not known; wires that end beside it: 1'b1, switch_2_p2
  BUS_DIPSWITCH bus_dipswitch_1 (.BUS_IN(undriven), .DISCONNECT(switch_2_p2), .BUS_OUT(bus_dipswitch_1_bus_out));
  CLOCK clock_1 (.CLK_SWITCH(switch_1_p2), .CLK_STEP(button_1_out), .CLK(clock_1_clk[16]));
  DotMatrix #(.inputtype("row"), .matrixcols(16), .matrixrows(1)) dotmatrix_1 (.row0(bus_dipswitch_1_bus_out));
  // DipSwitch #(.NSwitches(16)) dipswitch_2: pin names not known; wires that end beside it: PC_OUT, PCE, J, A_IN, A_OUT, A_RST, B_IN, B_OUT, B_RST, SU, F_RST, FI, EO, O_IN, O_RST, TWOS
  PROGRAM_COUNTER program_counter_1 (
    .BUS({clock_1_clk, bus_dipswitch_1_bus_out}), .PC_OUT(PC_OUT), .PCE(PCE), .J(J),
    .BUS_2({clock_1_clk, bus_dipswitch_1_bus_out}), .LEDS(program_counter_1_leds));
  REGISTER register_1 (
    .BUS({clock_1_clk, bus_dipswitch_1_bus_out}), .IN(A_IN), .OUT(A_OUT), .RST(A_RST),
    .A_BUS(register_1_a_bus), .LEDS(register_1_leds), .BUS_2({clock_1_clk, bus_dipswitch_1_bus_out}));
  DotMatrix #(.matrixcols(2), .matrixrows(1)) dotmatrix_2 (.col0(alu_1_cf), .col1(alu_1_zf));
  ALU alu_1 (
    .BUS({clock_1_clk, bus_dipswitch_1_bus_out}), .A_BUS(register_1_a_bus), .B_BUS(register_2_a_bus),
    .SU(SU), .F_RST(F_RST), .FI(FI), .EO(EO), .BUS_2({clock_1_clk, bus_dipswitch_1_bus_out}), .ZF(alu_1_zf),
    .CF(alu_1_cf), .LEDS(alu_1_leds));
  OUTPUT_7SEGMENT output_7segment_1 (
    .BUS({clock_1_clk, bus_dipswitch_1_bus_out}), .O_IN(O_IN), .O_RST(O_RST), .TWOS(TWOS),
    ._7SEGMENT(output_7segment_1__7segment), .NEG(output_7segment_1_neg));
  DotMatrix #(.matrixcols(1), .matrixrows(16)) dotmatrix_3 (.col0(program_counter_1_leds));
  DotMatrix #(.matrixcols(1), .matrixrows(16)) dotmatrix_4 (.col0(register_1_leds));
  DotMatrix #(.matrixcols(1), .matrixrows(16)) dotmatrix_5 (.col0(register_2_leds));
  DotMatrix #(.matrixcols(1), .matrixrows(16)) dotmatrix_6 (.col0(alu_1_leds));
  _7_Segment_Display u_7_segment_display_1 (
    .g(output_7segment_1_neg), .f(1'b0), .a(1'b0), .b(1'b0), .d(1'b0), .c(1'b0), .dp(1'b0));  // open: e
  REGISTER register_2 (
    .BUS({clock_1_clk, bus_dipswitch_1_bus_out}), .IN(B_IN), .OUT(B_OUT), .RST(B_RST),
    .A_BUS(register_2_a_bus), .LEDS(register_2_leds), .BUS_2({clock_1_clk, bus_dipswitch_1_bus_out}));
  _7_Segment_Display u_7_segment_display_2 (
    .g(output_7segment_1__7segment[3]), .f(output_7segment_1__7segment[2]),
    .a(output_7segment_1__7segment[1]), .b(output_7segment_1__7segment[0]),
    .e(output_7segment_1__7segment[7]), .d(output_7segment_1__7segment[6]),
    .c(output_7segment_1__7segment[5]), .dp(output_7segment_1__7segment[4]));
  _7_Segment_Display u_7_segment_display_3 (
    .g(output_7segment_1__7segment[11]), .f(output_7segment_1__7segment[10]),
    .a(output_7segment_1__7segment[9]), .b(output_7segment_1__7segment[8]),
    .e(output_7segment_1__7segment[15]), .d(output_7segment_1__7segment[14]),
    .c(output_7segment_1__7segment[13]), .dp(output_7segment_1__7segment[12]));
  _7_Segment_Display u_7_segment_display_4 (
    .g(output_7segment_1__7segment[19]), .f(output_7segment_1__7segment[18]),
    .a(output_7segment_1__7segment[17]), .b(output_7segment_1__7segment[16]),
    .e(output_7segment_1__7segment[23]), .d(output_7segment_1__7segment[22]),
    .c(output_7segment_1__7segment[21]), .dp(output_7segment_1__7segment[20]));
  _7_Segment_Display u_7_segment_display_5 (
    .g(output_7segment_1__7segment[27]), .f(output_7segment_1__7segment[26]),
    .a(output_7segment_1__7segment[25]), .b(output_7segment_1__7segment[24]),
    .e(output_7segment_1__7segment[31]), .d(output_7segment_1__7segment[30]),
    .c(output_7segment_1__7segment[29]), .dp(output_7segment_1__7segment[28]));

  // Notes on the sheet:
  //   CLK_STEP
  //   RST
  //   ALU
  //   PROGRAM_COUNTER
  //   A_REG
  //   B_REG
endmodule

module PROGRAM_COUNTER (
  input  [17:0] BUS,
  input  PC_OUT,
  input  PCE,
  input  J,
  output [15:0] LEDS,
  output [17:0] BUS_2
);

  wire pull_resistor_6_node;

  Pull_Resistor pull_resistor_1 (.node(BUS[17]));
  Pull_Resistor pull_resistor_2 (.node(PCE));
  Pull_Resistor pull_resistor_3 (.node(BUS[16]));
  Pull_Resistor pull_resistor_4 (.node(J));
  Pull_Resistor pull_resistor_5 (.node(PC_OUT));
  Pull_Resistor pull_resistor_6 (.node(pull_resistor_6_node));
  Counter #(.width(16), .max('hffff)) counter_1 (
    .load(J), .D(BUS[15:0]), .count(PCE), .Q(LEDS), .clk(BUS[16]), .clr(BUS[17]),
    .preset(pull_resistor_6_node), .down(pull_resistor_6_node));  // open: carry
  Pull_Resistor pull_resistor_7 (.node(LEDS));
  assign BUS_2[15:0] = PC_OUT ? LEDS : 16'bz;  // Controlled_Buffer controlled_buffer_1
endmodule

module REGISTER (
  input  [17:0] BUS,
  input  IN,
  input  OUT,
  input  RST,
  output [17:0] BUS_2,
  output [15:0] LEDS,
  output [15:0] A_BUS
);

  wire and_1_out, or_1_out, pull_resistor_3_node;

  or or_1 (or_1_out, BUS[17], and_1_out);
  and and_1 (and_1_out, BUS[16], RST);
  Pull_Resistor pull_resistor_1 (.node(IN));
  Pull_Resistor pull_resistor_2 (.node(OUT));
  Pull_Resistor pull_resistor_3 (.node(pull_resistor_3_node));
  Register #(.width(16), .Select("low")) register_1 (
    .D(BUS[15:0]), .en(IN), .Q(A_BUS), .clk(BUS[16]), .clr(or_1_out), .cs(pull_resistor_3_node),
    .preset(pull_resistor_3_node));
  Pull_Resistor pull_resistor_4 (.node(or_1_out));
  Pull_Resistor pull_resistor_5 (.node(A_BUS));
  assign BUS_2[15:0] = OUT ? A_BUS : 16'bz;  // Controlled_Buffer controlled_buffer_1

  assign LEDS = A_BUS;
endmodule

module ALU (
  input  [17:0] BUS,
  input  [15:0] A_BUS,
  input  [15:0] B_BUS,
  input  SU,
  input  F_RST,
  input  FI,
  input  EO,
  output ZF,
  output CF,
  output [15:0] LEDS,
  output [17:0] BUS_2
);

  wire adder_1_cout, and_1_out, nor_1_out, or_1_out, or_2_out, pull_resistor_4_node, pull_resistor_5_node,
       pull_resistor_6_node, pull_resistor_7_node, subtractor_1_bout;
  wire [15:0] adder_1_out, subtractor_1_out;

  and and_1 (and_1_out, BUS[16], F_RST);
  Pull_Resistor pull_resistor_1 (.node(FI));
  Pull_Resistor pull_resistor_2 (.node(EO));
  or or_1 (or_1_out, BUS[17], and_1_out);
  Pull_Resistor pull_resistor_3 (.node(SU));
  Pull_Resistor pull_resistor_4 (.node(pull_resistor_4_node));
  Adder #(.width(16)) adder_1 (
    .a(A_BUS), .b(B_BUS), .out(adder_1_out), .cin(pull_resistor_4_node), .cout(adder_1_cout));
  Pull_Resistor pull_resistor_5 (.node(pull_resistor_5_node));
  Subtractor #(.width(16)) subtractor_1 (
    .a(A_BUS), .b(B_BUS), .out(subtractor_1_out), .bin(pull_resistor_5_node), .bout(subtractor_1_bout));
  Pull_Resistor pull_resistor_6 (.node(pull_resistor_6_node));
  Register #(.width(1), .Select("low")) register_1 (
    .D(nor_1_out), .en(FI), .Q(ZF), .clk(BUS[16]), .clr(or_1_out), .cs(pull_resistor_6_node),
    .preset(pull_resistor_6_node));
  or or_2 (or_2_out, adder_1_cout, subtractor_1_bout);
  Pull_Resistor pull_resistor_7 (.node(pull_resistor_7_node));
  Register #(.width(1), .Select("low")) register_2 (
    .D(or_2_out), .en(FI), .Q(CF), .clk(BUS[16]), .clr(or_1_out), .cs(pull_resistor_7_node),
    .preset(pull_resistor_7_node));
  Multiplexer #(.width(16), .enable("false")) multiplexer_1 (
    .in0(adder_1_out), .in1(subtractor_1_out), .out(LEDS), .sel(SU));
  Pull_Resistor pull_resistor_8 (.node(LEDS));
  assign BUS_2[15:0] = EO ? LEDS : 16'bz;  // Controlled_Buffer controlled_buffer_1
  nor nor_1 (nor_1_out, LEDS[15], LEDS[14], LEDS[13], LEDS[12], LEDS[11], LEDS[10], LEDS[9], LEDS[8], LEDS[7], LEDS[6], LEDS[5], LEDS[4], LEDS[3], LEDS[2], LEDS[1], LEDS[0]);
endmodule

module BUS_DIPSWITCH (
  input  [15:0] BUS_IN,
  input  DISCONNECT,
  output [15:0] BUS_OUT
);

  Pull_Resistor pull_resistor_1 (.node(DISCONNECT));
  Pull_Resistor pull_resistor_2 (.node(BUS_IN[5]));
  Pull_Resistor pull_resistor_3 (.node(BUS_IN[1]));
  Pull_Resistor pull_resistor_4 (.node(BUS_IN[0]));
  Pull_Resistor pull_resistor_5 (.node(BUS_IN[6]));
  Pull_Resistor pull_resistor_6 (.node(BUS_IN[7]));
  Pull_Resistor pull_resistor_7 (.node(BUS_IN[2]));
  Pull_Resistor pull_resistor_8 (.node(BUS_IN[4]));
  Pull_Resistor pull_resistor_9 (.node(BUS_IN[3]));
  // Ttl74125 #(.ShowInternalStructure("true")) ttl74125_1: pin names not known; wires that end beside it: DISCONNECT, DISCONNECT, BUS_IN[15], BUS_IN[0], BUS_OUT[15], BUS_OUT[0], DISCONNECT
  Pull_Resistor pull_resistor_10 (.node(BUS_IN[12]));
  Pull_Resistor pull_resistor_11 (.node(BUS_IN[13]));
  Pull_Resistor pull_resistor_12 (.node(BUS_IN[11]));
  Pull_Resistor pull_resistor_13 (.node(BUS_IN[14]));
  Pull_Resistor pull_resistor_14 (.node(BUS_IN[8]));
  Pull_Resistor pull_resistor_15 (.node(BUS_IN[15]));
  Pull_Resistor pull_resistor_16 (.node(BUS_IN[9]));
  Pull_Resistor pull_resistor_17 (.node(BUS_IN[10]));
  // Ttl74125 #(.ShowInternalStructure("true")) ttl74125_2: pin names not known; wires that end beside it: DISCONNECT, BUS_IN[14], BUS_IN[1], BUS_OUT[14], BUS_OUT[1], DISCONNECT, DISCONNECT, BUS_IN[13], BUS_IN[2], BUS_OUT[13], BUS_OUT[2], DISCONNECT
  // Ttl74125 #(.ShowInternalStructure("true")) ttl74125_3: pin names not known; wires that end beside it: DISCONNECT, BUS_IN[12], BUS_IN[3], BUS_OUT[12], BUS_OUT[3], DISCONNECT, DISCONNECT, BUS_IN[11], BUS_IN[4], BUS_OUT[11], BUS_OUT[4], DISCONNECT
  // Ttl74125 #(.ShowInternalStructure("true")) ttl74125_4: pin names not known; wires that end beside it: DISCONNECT, BUS_IN[10], BUS_IN[5], BUS_OUT[10], BUS_OUT[5], DISCONNECT, DISCONNECT, BUS_IN[9], BUS_IN[6], BUS_OUT[9], BUS_OUT[6], DISCONNECT, DISCONNECT, BUS_IN[8], BUS_IN[7], BUS_OUT[8], BUS_OUT[7]

  // Other names for the same wires on the sheet: M0 = BUS_IN[0]; M1 = BUS_IN[1]; M2 = BUS_IN[2]; M3 = BUS_IN[3];
  //   M4 = BUS_IN[4]; M5 = BUS_IN[5]; M6 = BUS_IN[6]; M7 = BUS_IN[7]; M8 = BUS_IN[8]; M9 = BUS_IN[9];
  //   M10 = BUS_IN[10]; M11 = BUS_IN[11]; M12 = BUS_IN[12]; M13 = BUS_IN[13]; M14 = BUS_IN[14]; M15 = BUS_IN[15]
endmodule

module OUTPUT_7SEGMENT (
  input  [17:0] BUS,
  input  O_IN,
  input  O_RST,
  input  TWOS,
  output [31:0] _7SEGMENT,
  output NEG
);

  wire and_2_out, or_1_out, pull_resistor_4_node, pull_resistor_5_node;
  wire [15:0] register_1_q;

  Pull_Resistor pull_resistor_1 (.node(O_IN));
  Pull_Resistor pull_resistor_2 (.node(O_RST));
  Pull_Resistor pull_resistor_3 (.node(TWOS));
  // AND_Gate and_1 is placed but not wired
  or or_1 (or_1_out, BUS[17], and_2_out);
  and and_2 (and_2_out, BUS[16], O_RST);
  Pull_Resistor pull_resistor_4 (.node(pull_resistor_4_node));
  Register #(.width(16), .Select("low")) register_1 (
    .D(BUS[15:0]), .en(O_IN), .Q(register_1_q), .clk(BUS[16]), .clr(or_1_out), .cs(pull_resistor_4_node),
    .preset(pull_resistor_4_node));
  Pull_Resistor pull_resistor_5 (.node(pull_resistor_5_node));
  ROM #(.addrWidth(17), .dataWidth(32), .Select("low")) rom_1 (
    .addr({TWOS, register_1_q}), .data(_7SEGMENT), .sel(pull_resistor_5_node));

  assign NEG = TWOS;

  // Notes on the sheet:
  //   NEG
endmodule
